// Logisim project DrawCPU-8.circ as structural Verilog: 17 circuits, main circuit HalfAdder
module main (
  input  in_1,
  input  [7:0] in_2,
  input  CLK,
  input  in_4,
  output [7:0] out_5,
  output [7:0] out_6
);

  Mera_Register_8 mera_register_8_1 (.LD(in_1), .EN(in_4), .D(in_2), .CLK(CLK), .Q(out_5), .BS(out_6));
endmodule

module HalfAdder (
  input  A,
  input  B,
  output S,
  output C
);

  _7408 u_7408_1 (.pin10(B), .pin9(A), .pin8(C));  // open: pin1, pin2, pin3, pin4, pin5, pin6, pin13, pin12, pin11
  Mera_XOR mera_xor_1 (.A(A), .B(B), .O(S));
endmodule

module FullAdder (
  input  A,
  input  B,
  input  Cin,
  output S,
  output Cout
);

  wire halfadder_1_c, halfadder_1_s, n7432_1_pin9;

  HalfAdder halfadder_1 (.A(A), .B(B), .S(halfadder_1_s), .C(halfadder_1_c));
  _7432 u_7432_1 (
    .pin10(halfadder_1_c), .pin9(n7432_1_pin9), .pin8(Cout));  // open: pin1, pin2, pin3, pin4, pin5, pin6, pin13, pin12, pin11
  HalfAdder halfadder_2 (.A(halfadder_1_s), .B(Cin), .S(S), .C(n7432_1_pin9));
endmodule

module Mera_XOR (
  input  A,
  input  B,
  output O
);

  wire n7408_1_pin3, n7408_1_pin8, not_1_out, not_2_out;

  not not_1 (not_1_out, A);
  not not_2 (not_2_out, B);
  _7408 u_7408_1 (
    .pin1(not_1_out), .pin2(B), .pin3(n7408_1_pin3), .pin10(not_2_out), .pin9(A), .pin8(n7408_1_pin8));  // open: pin4, pin5, pin6, pin13, pin12, pin11
  _7432 u_7432_1 (
    .pin1(n7408_1_pin3), .pin2(n7408_1_pin8), .pin3(O));  // open: pin4, pin5, pin6, pin13, pin12, pin11, pin10, pin9, pin8
endmodule

module FFA (
  input  [3:0] A,
  input  [3:0] B,
  input  Cin,
  output [3:0] S,
  output Cout
);

  wire fulladder_1_cout, fulladder_2_cout, fulladder_3_cout;

  FullAdder fulladder_1 (.A(A[0]), .B(B[0]), .Cin(Cin), .S(S[0]), .Cout(fulladder_1_cout));
  FullAdder fulladder_2 (.A(A[2]), .B(B[2]), .Cin(fulladder_3_cout), .S(S[2]), .Cout(fulladder_2_cout));
  FullAdder fulladder_3 (.A(A[1]), .B(B[1]), .Cin(fulladder_1_cout), .S(S[1]), .Cout(fulladder_3_cout));
  FullAdder fulladder_4 (.A(A[3]), .B(B[3]), .Cin(fulladder_2_cout), .S(S[3]), .Cout(Cout));
endmodule

module EFA (
  input  [7:0] A,
  input  [7:0] B,
  input  Cin,
  output [7:0] Sum,
  output Cout
);

  wire ffa_1_cout;

  FFA ffa_1 (.A(A[3:0]), .B(B[3:0]), .Cin(Cin), .S(Sum[3:0]), .Cout(ffa_1_cout));
  FFA ffa_2 (.A(A[7:4]), .B(B[7:4]), .Cin(ffa_1_cout), .S(Sum[7:4]), .Cout(Cout));
endmodule

module AU (
  input  [7:0] A,
  input  [7:0] B,
  input  SE,
  output [7:0] S_D
);

  wire efa_1_cout;
  wire [7:0] mera_xor_3_o;

  Mera_XOR mera_xor_1 (.A(SE), .B(B[4]), .O(mera_xor_3_o[4]));
  Mera_XOR mera_xor_2 (.A(SE), .B(B[5]), .O(mera_xor_3_o[5]));
  Mera_XOR mera_xor_3 (.A(SE), .B(B[0]), .O(mera_xor_3_o[0]));
  Mera_XOR mera_xor_4 (.A(SE), .B(B[1]), .O(mera_xor_3_o[1]));
  Mera_XOR mera_xor_5 (.A(SE), .B(B[2]), .O(mera_xor_3_o[2]));
  Mera_XOR mera_xor_6 (.A(SE), .B(B[3]), .O(mera_xor_3_o[3]));
  Mera_XOR mera_xor_7 (.A(SE), .B(B[6]), .O(mera_xor_3_o[6]));
  EFA efa_1 (.A(A), .B(mera_xor_3_o), .Cin(SE), .Sum(S_D), .Cout(efa_1_cout));
  Mera_XOR mera_xor_8 (.A(SE), .B(B[7]), .O(mera_xor_3_o[7]));
  // NoConnect on efa_1_cout
endmodule

module ALU (
  input  [7:0] A,
  input  [7:0] B,
  input  SE,
  input  [2:0] SEL,
  output [7:0] O
);

  wire [7:0] and_1_out, au_1_s_d, mera_xor_8_1_o, nand_1_out, nor_1_out, not_1_out, not_2_out, or_1_out;

  assign not_1_out = ~B;  // NOT_Gate not_1, 8 bits wide
  AU au_1 (.A(A), .B(B), .SE(SE), .S_D(au_1_s_d));
  Mera_XOR_8 mera_xor_8_1 (.A(A), .B(B), .O(mera_xor_8_1_o));
  Multiplexer #(.select(3), .width(8)) multiplexer_1 (
    .in0(au_1_s_d), .in1(not_2_out), .in2(and_1_out), .in3(mera_xor_8_1_o), .in4(or_1_out), .in5(nand_1_out),
    .in6(nor_1_out), .in7(not_1_out), .out(O), .sel(SEL));
  assign and_1_out = A & B;  // AND_Gate and_1, 8 bits wide
  assign not_2_out = ~A;  // NOT_Gate not_2, 8 bits wide
  assign or_1_out = A | B;  // OR_Gate or_1, 8 bits wide
  assign nand_1_out = ~(A & B);  // NAND_Gate nand_1, 8 bits wide
  assign nor_1_out = ~(A | B);  // NOR_Gate nor_1, 8 bits wide
endmodule

module Mera_XOR_8 (
  input  [7:0] A,
  input  [7:0] B,
  output [7:0] O
);

  wire [7:0] and_1_out, and_2_out, not_1_out, not_2_out;

  assign not_1_out = ~A;  // NOT_Gate not_1, 8 bits wide
  assign not_2_out = ~B;  // NOT_Gate not_2, 8 bits wide
  assign and_1_out = not_1_out & B;  // AND_Gate and_1, 8 bits wide
  assign and_2_out = not_2_out & A;  // AND_Gate and_2, 8 bits wide
  assign O = and_1_out | and_2_out;  // OR_Gate or_1, 8 bits wide
endmodule

module SR_Latch (
  input  R,
  input  S,
  output Q,
  output Q_NOT
);

  _7436 u_7436_1 (.pin13(Q_NOT), .pin12(R), .pin11(Q));  // open: pin1, pin2, pin3, pin4, pin5, pin6, pin10, pin9, pin8
  _7436 u_7436_2 (.pin13(S), .pin12(Q), .pin11(Q_NOT));  // open: pin1, pin2, pin3, pin4, pin5, pin6, pin10, pin9, pin8
endmodule

module D_Latch (
  input  D,
  input  EN,
  output Q,
  output Q_NOT
);

  wire n7408_1_pin3, n7408_1_pin11, n7408_1_pin13;

  _7408 u_7408_1 (
    .pin1(EN), .pin2(D), .pin3(n7408_1_pin3), .pin13(n7408_1_pin13), .pin12(EN), .pin11(n7408_1_pin11));  // open: pin4, pin5, pin6, pin10, pin9, pin8
  not not_1 (n7408_1_pin13, D);
  SR_Latch sr_latch_1 (.R(n7408_1_pin11), .S(n7408_1_pin3), .Q(Q), .Q_NOT(Q_NOT));
endmodule

module D_FlipFlop (
  input  D,
  input  CLK,
  output Q,
  output Q_NOT
);

  wire d_latch_1_q, d_latch_1_q_not, not_1_out;

  not not_1 (not_1_out, CLK);
  D_Latch d_latch_1 (.D(D), .EN(CLK), .Q(d_latch_1_q), .Q_NOT(d_latch_1_q_not));
  // NoConnect on d_latch_1_q_not
  D_Latch d_latch_2 (.D(d_latch_1_q), .EN(not_1_out), .Q(Q), .Q_NOT(Q_NOT));
endmodule

module Mera_Register (
  input  LD,
  input  D,
  input  CLK,
  input  EN,
  output Q,
  output BS
);

  wire d_flipflop_1_q_not, d_flipflop_2_q, d_flipflop_2_q_not, n7408_1_pin3, n7408_1_pin11, n7408_1_pin13,
       n7432_1_pin11;

  _7408 u_7408_1 (
    .pin1(D), .pin2(LD), .pin3(n7408_1_pin3), .pin13(n7408_1_pin13), .pin12(Q), .pin11(n7408_1_pin11));  // open: pin4, pin5, pin6, pin10, pin9, pin8
  not not_1 (n7408_1_pin13, LD);
  _7432 u_7432_1 (
    .pin13(n7408_1_pin11), .pin12(n7408_1_pin3), .pin11(n7432_1_pin11));  // open: pin1, pin2, pin3, pin4, pin5, pin6, pin10, pin9, pin8
  D_FlipFlop d_flipflop_1 (.D(n7432_1_pin11), .CLK(CLK), .Q(Q), .Q_NOT(d_flipflop_1_q_not));
  // NoConnect on d_flipflop_1_q_not
  assign BS = d_flipflop_2_q ? Q : 1'bz;  // Controlled_Buffer controlled_buffer_1
  D_FlipFlop d_flipflop_2 (.D(EN), .CLK(CLK), .Q(d_flipflop_2_q), .Q_NOT(d_flipflop_2_q_not));
  // NoConnect on d_flipflop_2_q_not
endmodule

module Mera_Register_8 (
  input  LD,
  input  EN,
  input  [7:0] D,
  input  CLK,
  output [7:0] Q,
  output [7:0] BS
);

  Mera_Register mera_register_1 (.LD(LD), .D(D[0]), .CLK(CLK), .EN(EN), .Q(Q[0]), .BS(BS[0]));
  Mera_Register mera_register_2 (.LD(LD), .D(D[1]), .CLK(CLK), .EN(EN), .Q(Q[1]), .BS(BS[1]));
  Mera_Register mera_register_3 (.LD(LD), .D(D[2]), .CLK(CLK), .EN(EN), .Q(Q[2]), .BS(BS[2]));
  Mera_Register mera_register_4 (.LD(LD), .D(D[3]), .CLK(CLK), .EN(EN), .Q(Q[3]), .BS(BS[3]));
  Mera_Register mera_register_5 (.LD(LD), .D(D[4]), .CLK(CLK), .EN(EN), .Q(Q[4]), .BS(BS[4]));
  Mera_Register mera_register_6 (.LD(LD), .D(D[5]), .CLK(CLK), .EN(EN), .Q(Q[5]), .BS(BS[5]));
  Mera_Register mera_register_7 (.LD(LD), .D(D[6]), .CLK(CLK), .EN(EN), .Q(Q[6]), .BS(BS[6]));
  Mera_Register mera_register_8 (.LD(LD), .D(D[7]), .CLK(CLK), .EN(EN), .Q(Q[7]), .BS(BS[7]));
endmodule

module JK_FlipFlop (
  input  J,
  input  CLK,
  input  K,
  output Q,
  output Q_NOT
);

  J_K_Flip_Flop j_k_ff_1 (.J(J), .K(K), .clk(CLK), .Q(Q), .Qn(Q_NOT));  // open: preset, reset
endmodule

module Mera_RAM (
  input  [7:0] DIN,
  input  WR,
  input  RD,
  input  CLK,
  input  [3:0] ADDR,
  output [7:0] DOUT
);

  Mera_Register_8 mera_register_8_1 ();  // open: LD, EN, D, CLK, Q, BS
  Mera_Register_8 mera_register_8_2 ();  // open: LD, EN, D, CLK, Q, BS
  Mera_Register_8 mera_register_8_3 ();  // open: LD, EN, D, CLK, Q, BS
  Mera_Register mera_register_1 ();  // open: LD, D, CLK, EN, Q, BS
  Mera_Register mera_register_2 ();  // open: LD, D, CLK, EN, Q, BS
  Mera_Register_8 mera_register_8_4 ();  // open: LD, EN, D, CLK, Q, BS
  Mera_Register_8 mera_register_8_5 ();  // open: LD, EN, D, CLK, Q, BS
  Mera_Register_8 mera_register_8_6 ();  // open: LD, EN, D, CLK, Q, BS
  Mera_Register mera_register_3 ();  // open: LD, D, CLK, EN, Q, BS
  Mera_Register mera_register_4 ();  // open: LD, D, CLK, EN, Q, BS
  Mera_Register_8 mera_register_8_7 ();  // open: LD, EN, D, CLK, Q, BS
  Mera_Register_8 mera_register_8_8 ();  // open: LD, EN, D, CLK, Q, BS
  Mera_Register_8 mera_register_8_9 ();  // open: LD, EN, D, CLK, Q, BS
  Mera_Register_8 mera_register_8_10 ();  // open: LD, EN, D, CLK, Q, BS
  Mera_Register mera_register_5 ();  // open: LD, D, CLK, EN, Q, BS
  Mera_Register mera_register_6 ();  // open: LD, D, CLK, EN, Q, BS
  // L_74LS154_ea18d7cc l_74ls154_ea18d7cc_1: pin names not known
endmodule

module AddressDecoder_4to16 (
  input  [3:0] ADDR,
  output A0,
  output A1,
  output A2,
  output out_5,
  output out_6,
  output out_7,
  output out_8,
  output out_9,
  output out_10,
  output out_11,
  output out_12,
  output out_13,
  output out_14,
  output out_15,
  output out_16
);

  wire not_1_out, not_2_out, not_3_out, not_4_out;

  not not_1 (not_1_out, ADDR[1]);
  not not_2 (not_2_out, ADDR[1]);
  not not_3 (not_3_out, ADDR[2]);
  not not_4 (not_4_out, ADDR[3]);
  and and_1 (A0, ADDR[1], ADDR[1], ADDR[2], ADDR[3]);
  and and_2 (A1, not_1_out, ADDR[1], ADDR[2], ADDR[3]);
  and and_3 (A2, ADDR[1], not_2_out, ADDR[2], ADDR[3]);
  buf and_4 (out_6, not_3_out);  // AND_Gate
  // AND_Gate and_5 has open pins: in3=not_4_out, out=open
  // AND_Gate and_6 is placed but not wired
  // AND_Gate and_7 is placed but not wired
  // AND_Gate and_8 is placed but not wired
  // AND_Gate and_9 is placed but not wired
  // AND_Gate and_10 is placed but not wired
  // AND_Gate and_11 is placed but not wired
  // AND_Gate and_12 is placed but not wired
  // AND_Gate and_13 is placed but not wired
  // AND_Gate and_14 is placed but not wired
  // AND_Gate and_15 is placed but not wired
  // AND_Gate and_16 is placed but not wired

  assign ADDR[0] = ADDR[1];
endmodule
